# Fritzing sketch arduino (saved by Fritzing 0.9.9b)

parts:
  Componente1 = Arduino Uno (Rev3)
  U1 = PIC-ICSP-Mini [part_number=CN1 package=pic-icsp-mini]
  JP5 = Header 4 [package=jst-4-pth]
  Componente2 = Adafruit INA219 Current Sensor FeatherWing [part_number=3650]  # not connected
  hc-sr3 = HC-SR04 Ultrasonic Distance Sensor
  hc-sr2 = HC-SR04 Ultrasonic Distance Sensor
  hc-sr1 = HC-SR04 Ultrasonic Distance Sensor

nets:
  N1: Componente1.A4/SDA, JP5.3
  N2: Componente1.A5/SCL, JP5.4
  GND: Componente1.GND, U1.PGD, JP5.2, hc-sr3.GND, hc-sr2.GND, hc-sr1.GND
  N3: Componente1.D4, hc-sr3.ECHO
  N4: Componente1.D5_PWM, hc-sr2.ECHO
  N5: Componente1.D6_PWM, hc-sr1.ECHO
  N6: Componente1.D7, hc-sr2.TRIG, hc-sr1.TRIG
  VCC: Componente1.5V, hc-sr3.VCC, hc-sr2.VCC, hc-sr1.VCC
  N7: Componente1.VIN, U1.PGC

notes:
  +12V In
  +12V in
  I2C Connector

custom parts:
  Adafruit INA219 Current Sensor FeatherWing: The INA219 FeatherWing makes power-monitoring problems a thing of the past. Use the handy INA219B chip on this breakout to both measure both the high side voltage and DC current draw over I2C with 1% precision. Works with any and all Feathers! Communicates over I2C so its super-simple to use, you can even change the I2C address to have up to 4 of these Wings on one Feather. This chip can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

// code stored in the sketch: test.ino
#include <Wire.h>

#define SLAVE_ADDRESS 0x30
#define TOTAL_SENSORS 3

#define TRIG  7
#define ECHO1 6
#define ECHO2 5
#define ECHO3 4

unsigned long maxloops;

long timesStart[TOTAL_SENSORS];
long timesStop[TOTAL_SENSORS];
int  distances[TOTAL_SENSORS];
uint8_t bits[TOTAL_SENSORS];

void setup()
{
  Wire.begin(SLAVE_ADDRESS);
  Wire.onRequest(requestEvent); // register event
  Wire.onReceive(receiveData);
  Serial.begin(9600);
  
  DDRD = 0x80; //All bits as INPUT except TRIG (7)  
  for (int n=0;n<TOTAL_SENSORS;n++) {
    bits[n] = 0x40 >> n;
  }
  maxloops = microsecondsToClockCycles(500);
}

void loop()
{      
  memset (timesStart, 0, sizeof(timesStart));
  memset (timesStop, 0, sizeof(timesStop));
  
  digitalWrite(TRIG, LOW);
  delayMicroseconds(2);
  digitalWrite(TRIG, HIGH);
  delayMicroseconds(10);
  digitalWrite(TRIG, LOW);
  
  unsigned long numloops=0;
  uint8_t val;
  uint8_t count=0;
  
  while (count < TOTAL_SENSORS && numloops < maxloops) {
    val= *portInputRegister(digitalPinToPort(ECHO1));
    for (int n=0;n<TOTAL_SENSORS; n++) {
      if ( (val & bits[n]) == LOW ) {
        if ( timesStart[n] == 0) {          
          timesStop[n]=0;
        } else if (timesStop[n] == 0) { 
            timesStop[n]=micros()-timesStart[n];
            count++;          
          }        
      } else if (timesStart[n]==0) {  //HIGH        
          timesStart[n]=micros();
      }
    }
    numloops++;
  };

  Serial.print ("Distance : ");
  for (int n=0; n<TOTAL_SENSORS; n++) {
    distances[n] = (timesStop[n] * 0.034) / 2;
    Serial.print (distances[n]);
    Serial.print (" ");
  }  
  Serial.println (" ");
  delay(100);
}

// function that executes whenever data is requested by master
// this function is registered as an event, see setup()
void requestEvent()
{
  for (int n=0; n<TOTAL_SENSORS; n++)
    Wire.write (distances[n]);
    
}

void receiveData(int byteCount)
{
}
